// Logisim project ULA de 1 bit.circ as structural Verilog: 1 circuit, main circuit main
module main (
  input  vem_um,
  input  inv_a,
  input  a,
  input  en_a,
  input  b,
  input  en_b,
  input  f0,
  input  f1,
  output saida,
  output vai_um
);

  wire and_1_out, and_2_out, and_3_out, and_4_out, and_5_out, and_6_out, and_7_out, and_8_out, and_9_out,
       and_10_out, and_11_out, and_12_out, and_13_out, not_1_out, not_2_out, not_3_out, not_4_out, not_5_out,
       or_1_out, xor_1_out, xor_2_out, xor_3_out;

  and and_1 (and_1_out, a, en_a);
  and and_2 (and_2_out, b, b, en_b);
  not not_1 (not_1_out, f0);
  not not_2 (not_2_out, f1);
  not not_3 (not_3_out, f0);
  not not_4 (not_4_out, f1);
  xor xor_1 (xor_1_out, inv_a, and_1_out);
  and and_3 (and_3_out, not_1_out, not_2_out);
  and and_4 (and_4_out, not_3_out, f1);
  and and_5 (and_5_out, f0, not_4_out);
  and and_6 (and_6_out, f1, f0);
  and and_7 (and_7_out, xor_1_out, and_2_out);
  or or_1 (or_1_out, xor_1_out, and_2_out);
  not not_5 (not_5_out, and_2_out);
  and and_8 (and_8_out, and_7_out, and_3_out);
  and and_9 (and_9_out, or_1_out, and_4_out);
  and and_10 (and_10_out, not_5_out, and_5_out);
  and and_11 (and_11_out, and_6_out, xor_1_out, and_2_out);
  xor xor_2 (xor_2_out, xor_1_out, and_2_out);
  or or_2 (vai_um, and_11_out, and_12_out);
  and and_12 (and_12_out, vem_um, xor_2_out, and_6_out);
  xor xor_3 (xor_3_out, vem_um, xor_2_out);
  and and_13 (and_13_out, xor_3_out, and_6_out);
  or or_3 (saida, and_8_out, and_9_out, and_10_out, and_13_out);
endmodule
